# Fritzing sketch pin_mapping (saved by Fritzing 0.9.4)
breadboards: 2

parts:
  U1 = NodeMCU V3.0
  J2 = female pin header, 4 pins [form="♀ (female)"]
  SW1 = DIP SWITCH [package=dipswitch-02]
  J1 = female pin header, 5 pins [form="♀ (female)"]

nets:
  N1: U1.D1, J2.pin1
  N2: U1.D2, J2.pin2
  N3: U1.3V3, J2.pin4
  N4: U1.GND#6, U1.GND#13, U1.GND#16, U1.GND#33, J2.pin3, J1.pin3
  N5: U1.RX, SW1.2
  N6: U1.TX, SW1.1
  N7: U1.Vin, J1.pin4, J1.pin5
  N8: SW1.3, J1.pin2
  N9: SW1.4, J1.pin1

notes:
  BME280
  PMS7003
  SDA/SCL/GND/3.3V
  RX/TX/GND/5V/SET

custom parts:
  NodeMCU V3.0: ESP8266 based NodeMCU
